// Logisim project Final_Schematic_Involving_Sum_Function.circ as structural Verilog: 1 circuit, main circuit main
// 3
module main (
  input  C_in,
  input  [3:0] X,
  input  [3:0] Y,
  input  [1:0] mod_X,
  input  [1:0] mod_Y,
  output [4:0] SUMA_Z,
  output [2:0] SUMA_mod_Z,
  output [1:0] mod_Z_dolne,
  output [1:0] mod_Z_gorne
);

  wire and_1_out, and_2_out, and_3_out, and_4_out, and_5_out, and_6_out, and_7_out, and_8_out, and_9_out,
       and_10_out, and_11_out, and_13_out, and_14_out, and_15_out, and_16_out, and_17_out, and_18_out,
       and_19_out, and_20_out, and_21_out, and_22_out, and_23_out, and_24_out, not_1_out, not_2_out,
       not_4_out, not_5_out, not_6_out, not_7_out, not_8_out, not_9_out, not_10_out, not_11_out, not_12_out,
       or_1_out, or_3_out, or_4_out, or_5_out, or_7_out, or_8_out, or_9_out, or_10_out, xor_1_out, xor_3_out,
       xor_6_out, xor_8_out, xor_9_out, xor_10_out, xor_12_out, xor_13_out, xor_15_out, xor_16_out,
       xor_17_out, xor_18_out, xor_19_out, xor_20_out, xor_21_out, xor_22_out, xor_23_out;

  xor xor_1 (xor_1_out, X[0], Y[0]);
  and and_1 (and_1_out, X[0], Y[0]);
  and and_2 (and_2_out, mod_X[0], mod_Y[0]);
  xor xor_2 (SUMA_Z[0], C_in, xor_1_out);
  and and_3 (and_3_out, xor_1_out, C_in);
  and and_4 (and_4_out, mod_Y[1], mod_X[1]);
  xor xor_3 (xor_3_out, mod_X[1], mod_Y[1]);
  and and_5 (and_5_out, and_2_out, xor_3_out);
  or or_1 (or_1_out, and_3_out, and_1_out);
  or or_2 (SUMA_mod_Z[2], and_4_out, and_5_out);
  xor xor_4 (SUMA_mod_Z[1], xor_3_out, and_2_out);
  xor xor_5 (SUMA_mod_Z[0], mod_X[0], mod_Y[0]);
  xor xor_6 (xor_6_out, X[1], Y[1]);
  and and_6 (and_6_out, X[1], Y[1]);
  not not_1 (not_1_out, SUMA_mod_Z[1]);
  xor xor_7 (SUMA_Z[1], or_1_out, xor_6_out);
  and and_7 (and_7_out, xor_6_out, or_1_out);
  xor xor_8 (xor_8_out, SUMA_mod_Z[0], not_1_out);
  and and_8 (and_8_out, SUMA_mod_Z[0], not_1_out);
  or or_3 (or_3_out, and_7_out, and_6_out);
  and and_9 (and_9_out, xor_8_out, SUMA_mod_Z[2]);
  xor xor_9 (xor_9_out, xor_8_out, SUMA_mod_Z[2]);
  or or_4 (or_4_out, and_9_out, and_8_out);
  xor xor_10 (xor_10_out, X[2], Y[2]);
  and and_10 (and_10_out, X[2], Y[2]);
  xor xor_11 (SUMA_Z[2], or_3_out, xor_10_out);
  and and_11 (and_11_out, xor_10_out, or_3_out);
  or or_5 (or_5_out, and_11_out, and_10_out);
  not not_2 (not_2_out, xor_9_out);
  and and_12 (mod_Z_dolne[0], not_2_out, or_4_out);
  xor xor_12 (xor_12_out, xor_9_out, or_4_out);
  not not_3 (mod_Z_dolne[1], xor_12_out);
  xor xor_13 (xor_13_out, X[3], Y[3]);
  and and_13 (and_13_out, X[3], Y[3]);
  xor xor_14 (SUMA_Z[3], or_5_out, xor_13_out);
  and and_14 (and_14_out, xor_13_out, or_5_out);
  or or_6 (SUMA_Z[4], and_14_out, and_13_out);
  not not_4 (not_4_out, mod_Z_gorne[0]);
  not not_5 (not_5_out, SUMA_Z[3]);
  not not_6 (not_6_out, mod_Z_dolne[0]);
  and and_15 (and_15_out, not_4_out, mod_Z_gorne[1]);
  xor xor_15 (xor_15_out, and_15_out, and_16_out);
  not not_7 (not_7_out, SUMA_Z[1]);
  and and_16 (and_16_out, not_6_out, mod_Z_dolne[1]);
  not not_8 (not_8_out, mod_Z_dolne[1]);
  and and_17 (and_17_out, not_8_out, mod_Z_dolne[0]);
  or or_7 (or_7_out, xor_15_out, xor_16_out);
  LED led_1 (.in(or_7_out));
  not not_9 (not_9_out, mod_Z_gorne[1]);
  and and_18 (and_18_out, not_9_out, mod_Z_gorne[0]);
  xor xor_16 (xor_16_out, and_17_out, and_18_out);
  xor xor_17 (xor_17_out, SUMA_Z[0], not_7_out);
  and and_19 (and_19_out, SUMA_Z[0], not_7_out);
  and and_20 (and_20_out, xor_17_out, SUMA_Z[2]);
  xor xor_18 (xor_18_out, xor_17_out, SUMA_Z[2]);
  or or_8 (or_8_out, and_20_out, and_19_out);
  not not_10 (not_10_out, or_8_out);
  xor xor_19 (xor_19_out, xor_18_out, not_10_out);
  and and_21 (and_21_out, xor_18_out, not_10_out);
  and and_22 (and_22_out, xor_19_out, not_5_out);
  xor xor_20 (xor_20_out, xor_19_out, not_5_out);
  or or_9 (or_9_out, and_22_out, and_21_out);
  not not_11 (not_11_out, or_9_out);
  and and_23 (and_23_out, xor_20_out, not_11_out);
  xor xor_21 (xor_21_out, xor_20_out, not_11_out);
  xor xor_22 (xor_22_out, xor_21_out, SUMA_Z[4]);
  and and_24 (and_24_out, xor_21_out, SUMA_Z[4]);
  or or_10 (or_10_out, and_24_out, and_23_out);
  not not_12 (not_12_out, xor_22_out);
  and and_25 (mod_Z_gorne[0], not_12_out, or_10_out);
  xor xor_23 (xor_23_out, xor_22_out, or_10_out);
  not not_13 (mod_Z_gorne[1], xor_23_out);

  // Notes on the sheet:
  //   SUMATOR KASKADOWY
  //   SUMATOR KASKADOWY
  //   GENERATOR RESZTY
  //   KOREKCJA
  //   |Z|
  //   LSB
  //   MSB
  //   |Z|
  //   Z
  //   LSB
  //   MSB
  //   GENERATOR RESZTY MOD 3
  //   Z
  //   KOREKCJA
endmodule
