// Logisim project genresztmod3_togit.circ as structural Verilog: 4 circuits, main circuit main
module main (
  input  [4:0] X,
  input  [5:0] X2
);

  wire and_1_out, and_2_out, and_3_out, fulladder_1_c_out, fulladder_1_s, fulladder_2_c_out, fulladder_2_s,
       fulladder_3_c_out, fulladder_3_s, fulladder_4_c_out, fulladder_4_s, fulladder_5_c_out, fulladder_5_s,
       fulladder_6_c_out, fulladder_6_s, fulladder_7_c_out, fulladder_7_s, not_1_out, not_2_out, not_3_out,
       not_4_out, not_5_out, not_6_out, not_7_out, not_8_out, not_9_out, not_10_out, not_11_out, not_12_out,
       not_13_out, not_14_out, wyjsciedlanieparzystejn_1_s0, wyjsciedlanieparzystejn_1_s1,
       wyjsciedlaparzystejn_1_s0, wyjsciedlaparzystejn_1_s1, xor_1_out;

  not not_1 (not_1_out, X2[1]);
  not not_2 (not_2_out, X2[3]);
  not not_3 (not_3_out, X2[5]);
  not not_4 (not_4_out, X[1]);
  FullAdder fulladder_1 (.B(not_1_out), .A(X2[0]), .C_in(X2[2]), .S(fulladder_1_s), .C_out(fulladder_1_c_out));
  FullAdder fulladder_2 (.B(X2[4]), .A(not_2_out), .C_in(not_3_out), .S(fulladder_2_s), .C_out(fulladder_2_c_out));
  FullAdder fulladder_3 (.B(not_4_out), .A(X[0]), .C_in(X[2]), .S(fulladder_3_s), .C_out(fulladder_3_c_out));
  not not_5 (not_5_out, fulladder_3_c_out);
  not not_6 (not_6_out, X[3]);
  not not_7 (not_7_out, fulladder_1_c_out);
  FullAdder fulladder_4 (
    .B(not_7_out), .A(fulladder_1_s), .C_in(fulladder_2_s), .S(fulladder_4_s), .C_out(fulladder_4_c_out));
  FullAdder fulladder_5 (
    .B(not_5_out), .A(fulladder_3_s), .C_in(not_6_out), .S(fulladder_5_s), .C_out(fulladder_5_c_out));
  not not_8 (not_8_out, fulladder_5_c_out);
  not not_9 (not_9_out, fulladder_4_c_out);
  not not_10 (not_10_out, fulladder_2_c_out);
  FullAdder fulladder_6 (
    .B(not_9_out), .A(fulladder_4_s), .C_in(not_10_out), .S(fulladder_6_s), .C_out(fulladder_6_c_out));
  FullAdder fulladder_7 (.B(not_8_out), .A(fulladder_5_s), .C_in(X[4]), .S(fulladder_7_s), .C_out(fulladder_7_c_out));
  not not_11 (not_11_out, fulladder_6_s);
  not not_12 (not_12_out, fulladder_7_s);
  and and_1 (and_1_out, fulladder_6_s, not_13_out);
  not not_13 (not_13_out, fulladder_6_c_out);
  and and_2 (and_2_out, not_11_out, fulladder_6_c_out);
  LED led_1 (.in(wyjsciedlaparzystejn_1_s0));
  WyjscieDlaParzystejN wyjsciedlaparzystejn_1 (
    .Sout_2kn(fulladder_6_s), .Cout(fulladder_6_c_out), .S1(wyjsciedlaparzystejn_1_s1),
    .S0(wyjsciedlaparzystejn_1_s0));
  LED led_2 (.in(wyjsciedlaparzystejn_1_s1));
  and and_3 (and_3_out, not_12_out, fulladder_7_c_out);
  xor xor_1 (xor_1_out, fulladder_7_s, fulladder_7_c_out);
  not not_14 (not_14_out, xor_1_out);
  WyjscieDlaNieparzystejN wyjsciedlanieparzystejn_1 (
    .Sout_2kplus1n(fulladder_7_s), .Cout(fulladder_7_c_out), .S0(wyjsciedlanieparzystejn_1_s0),
    .S1(wyjsciedlanieparzystejn_1_s1));
  LED led_3 (.in(and_1_out));
  LED led_4 (.in(and_2_out));
  LED S0 (.in(and_3_out));
  LED S1 (.in(not_14_out));
  LED led_5 (.in(wyjsciedlanieparzystejn_1_s0));
  LED led_6 (.in(wyjsciedlanieparzystejn_1_s1));

  // Notes on the sheet:
  //   DLA n = 2k + 1
  //   DLA n = 2k
  //   MODUL ZASTEPCZY
endmodule

module FullAdder (
  input  A,
  input  B,
  input  C_in,
  output S,
  output C_out
);

  wire and_1_out, and_2_out, xor_1_out;

  xor xor_1 (xor_1_out, A, B);
  and and_1 (and_1_out, A, B);
  xor xor_2 (S, xor_1_out, C_in);
  and and_2 (and_2_out, xor_1_out, C_in);
  or or_1 (C_out, and_2_out, and_1_out);
endmodule

module WyjscieDlaNieparzystejN (
  input  Sout_2kplus1n,
  input  Cout,
  output S0,
  output S1
);

  wire not_1_out, xor_1_out;

  not not_1 (not_1_out, Sout_2kplus1n);
  xor xor_1 (xor_1_out, Sout_2kplus1n, Cout);
  and and_1 (S0, not_1_out, Cout);
  not not_2 (S1, xor_1_out);
endmodule

module WyjscieDlaParzystejN (
  input  Sout_2kn,
  input  Cout,
  output S0,
  output S1
);

  wire not_1_out, not_2_out;

  not not_1 (not_1_out, Cout);
  not not_2 (not_2_out, Sout_2kn);
  and and_1 (S0, Sout_2kn, not_1_out);
  and and_2 (S1, not_2_out, Cout);
endmodule
